# Fritzing sketch Sketch (saved by Fritzing 0.8.7b)
breadboards: 1

parts:
  OLED1 = SSD1306 0.96in 128x64 I2C Monochrome OLED Display
  M1 = GY-MAX30102
  TP1 = TP4056 [chip_label=TP4056 package="DIP (Dual Inline) [THT]"]
  U2 = LuaNode32 / ESP32
  VCC1 = Battery  # not connected

nets:
  GND: OLED1.GND, M1.GND, TP1.pin6, U2.GND
  VCC: OLED1.VCC, M1.VIN, U2.3V3
  N1: OLED1.SCL, M1.SCL, U2.TX0
  N2: OLED1.SDA, M1.SDA, U2.D2
  N3: TP1.pin3, U2.Vin

custom parts:
  GY-MAX30102: Oximeter module using the MAX30102 chip. You may wish to read (and check your module) this post on power problems with these modules: https://reedpaper.wordpress.com/2018/08/22/pulse-oximeter-max30100-max30102-how-to-fix-wrong-board/ (may not apply as this is a different module!). As usual, if you want the mounting holes in pcb, you need to drag a hole over the pad in silkscreen to actually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
  TP4056: A DIP stand-in part for whatever IC you want. With 6 pins on a 300mil dual inline package (DIP) footprint.
  LuaNode32 / ESP32: ESP32 based LuaNode32
